# Fritzing sketch DFPlayer (saved by Fritzing 0.9.4)

parts:
  DFRobot_DFPlayer_Mini1 = DFRobot DFPlayer Mini [part_number=DFR0299]
  D1 = Rectifier Diode [part_number=1N4001 package="300 mil [THT]"]
  JACK3 = 2.1mm Barrel Jack with Terminal Block
  C1 = Electrolytic Capacitor [capacitance=1µF package="100 mil [THT, electrolytic]"]
  R1 = Resistor [tolerance=±5% resistance=1k package=THT]
  Part1 = Arduino Nano (Rev3.0)
  SP1 = SPEAKER [package=pcb_mount_speaker]

nets:
  N1: DFRobot_DFPlayer_Mini1.VCC, D1.cathode
  N2: DFRobot_DFPlayer_Mini1.RX, R1.Pin_0
  N3: DFRobot_DFPlayer_Mini1.TX, Part1.D2
  N4: DFRobot_DFPlayer_Mini1.SPK_1, SP1.-
  N5: DFRobot_DFPlayer_Mini1.SPK_2, SP1.+
  N6: DFRobot_DFPlayer_Mini1.GND-2, JACK3.NEG, C1.-, Part1.GND
  N7: D1.anode, JACK3.POS
  N8: R1.Pin_1, Part1.D3

notes:
  5V DC
  1kΩ
  6.3V, 1000uF
