# Fritzing sketch DY-SV17F (saved by Fritzing 0.9.4)

parts:
  J2 = rounded female pin header, 9 pins [form="♀ (female rounded)"]
  R1 = Resistor [tolerance=±5% resistance=10k package=THT]
  R2 = Resistor [tolerance=±5% resistance=10k package=THT]
  R3 = Resistor [tolerance=±5% resistance=10k package=THT]
  Part2 = Arduino Nano (Rev3.0)
  SP1 = SPEAKER [package=pcb_mount_speaker]
  R4 = Resistor [tolerance=±5% resistance=1k package="0603 [SMD]"]
  J1 = rounded female pin header, 9 pins [form="♀ (female rounded)"]
  U1 = ESP32S-HiLetgo [part_number=ESP32S-HiLetgo]
  R5 = Resistor [tolerance=±5% resistance=10k package=THT]  # not connected
  R6 = Resistor [tolerance=±5% resistance=10k package=THT]
  R7 = Resistor [tolerance=±5% resistance=10k package=THT]
  SP2 = SPEAKER [package=pcb_mount_speaker]  # not connected

nets:
  N1: J2.pin4, Part2.VIN
  N2: J2.pin5, R3.Pin_0
  N3: J2.pin8, SP1.+
  N4: J2.pin9, SP1.-
  N5: R1.Pin_0, R2.Pin_0, Part2.GND, J1.pin1
  N6: Part2.D8, J1.pin9
  N7: Part2.D9, R4.Pin_1
  N8: R4.Pin_0, J1.pin8
  N9: U1.GND, R6.Pin_0, R7.Pin_0

notes:
  If connecting to a 5V MCU like an Arduino Nano, include a 1kΩ resistor in series with the Rx line
  Operating mode is determined by HIGH/LOW state of CON1/2/3 pins.
  UART mode is set by LOW/LOW/HIGH
  - LOW is connected to GND via 10kΩ resistor
  - HIGH is 3.3V via 10kΩ resistor.
  (The module outputs 3.3V viapin 14 which can be used as reference)
  LLL = Momentary play song indexed by binary
  LLH = Latched play song index by binary
  (i.e. 11111010 plays track 00005.mp3
  00000000 plays track 00255.mp3)
  LHL = Momentary play song indexed by IO
  LHH = Latched play song index by IO
  (i.e. 11101111 plays track 00005.mp3
  01111111 plays track 00008.mp3)
  HLL = Serial interface mode
  HLH = MP3 Player mode

custom parts:
  ESP32S-HiLetgo: HiLetgo ESP-WROOM-32 ESP32 ESP-32S Development Board 2.4GHz Dual-Mode WiFi + Bluetooth Dual Cores Microcontroller The ESP32 integrated with Antenna switches, RF Balun, power amplifiers, low-noise amplifiers, filters, and management modules, and the entire solution occupies the least area of PCB. 2.4 GHz Wi-Fi plus Bluetooth dual-mode chip, with TSMC Ultra-low power consumption 40nm technology,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
